// Logisim project Laboratorio 1 - Circuito en Logisim.circ as structural Verilog: 1 circuit, main circuit main
module main (
  input  A,
  input  D3,
  input  B,
  input  A_2,
  input  D2,
  input  D1,
  input  B_2,
  input  A_3,
  input  D0,
  input  B_3,
  input  I0,
  input  I1,
  input  C,
  input  I2,
  input  I3,
  input  D,
  input  I4,
  input  I5,
  input  I6,
  input  I7,
  input  S2,
  input  S1,
  input  S0,
  output F___A___B,
  output XOR
);

  wire and_2_out, and_3_out, and_4_out, and_5_out, and_6_out, and_7_out, and_8_out, and_9_out, and_10_out,
       and_11_out, and_12_out, and_13_out, and_14_out, and_15_out, and_16_out, and_17_out, and_18_out,
       and_19_out, and_20_out, and_21_out, and_22_out, and_23_out, and_24_out, and_25_out, and_26_out,
       and_27_out, and_28_out, not_1_out, not_2_out, not_3_out, not_4_out, not_5_out, not_6_out, not_7_out,
       not_8_out, not_9_out, not_10_out, not_11_out, not_12_out, not_13_out, or_2_out, or_3_out, or_4_out,
       or_5_out;

  not not_1 (not_1_out, A_2);
  not not_2 (not_2_out, B_2);
  not not_3 (not_3_out, A_3);
  not not_4 (not_4_out, B_3);
  not not_5 (not_5_out, C);
  not not_6 (not_6_out, D);
  and and_1 (F___A___B, A, B);
  and and_2 (and_2_out, A_2, not_2_out);
  and and_3 (and_3_out, not_1_out, B_2);
  or or_1 (XOR, and_2_out, and_3_out);
  and and_4 (and_4_out, not_3_out, not_4_out, not_5_out, not_6_out);
  and and_5 (and_5_out, not_3_out, not_4_out, not_5_out, D);
  and and_6 (and_6_out, not_3_out, not_4_out, C, not_6_out);
  and and_7 (and_7_out, not_3_out, not_4_out, C, D);
  and and_8 (and_8_out, not_3_out, B_3, not_5_out, not_6_out);
  and and_9 (and_9_out, not_3_out, B_3, not_5_out, D);
  and and_10 (and_10_out, not_3_out, B_3, C, not_6_out);
  and and_11 (and_11_out, not_3_out, B_3, C, D);
  and and_12 (and_12_out, A_3, not_4_out, not_5_out, not_6_out);
  and and_13 (and_13_out, A_3, not_4_out, not_5_out, D);
  and and_14 (and_14_out, A_3, not_4_out, C, not_6_out);
  and and_15 (and_15_out, A_3, not_4_out, C, D);
  and and_16 (and_16_out, A_3, B_3, not_5_out, not_6_out);
  and and_17 (and_17_out, A_3, B_3, not_5_out, D);
  and and_18 (and_18_out, A_3, B_3, C, not_6_out);
  and and_19 (and_19_out, A_3, B_3, C, D);
  not not_7 (not_7_out, not_8_out);
  not not_8 (not_8_out, S2);
  not not_9 (not_9_out, not_10_out);
  not not_10 (not_10_out, S1);
  not not_11 (not_11_out, D2);
  not not_12 (not_12_out, not_13_out);
  not not_13 (not_13_out, S0);
  or or_2 (or_2_out, D3, D2);
  and and_20 (and_20_out, I0, not_7_out, not_9_out, not_12_out);
  and and_21 (and_21_out, I1, not_8_out, not_9_out, not_9_out, not_12_out);
  and and_22 (and_22_out, I2, not_9_out, not_12_out, not_10_out);
  and and_23 (and_23_out, I3, not_8_out, not_10_out, not_9_out, not_12_out);
  and and_24 (and_24_out, I4, not_7_out, not_9_out, not_13_out);
  and and_25 (and_25_out, I5, not_8_out, not_9_out, not_13_out);
  and and_26 (and_26_out, I6, not_7_out, not_10_out, not_13_out);
  and and_27 (and_27_out, I7, not_8_out, not_10_out, not_13_out);
  and and_28 (and_28_out, not_11_out, D1);
  or or_3 (or_3_out, or_2_out, D1, D0);
  or or_4 (or_4_out, D3, and_28_out);
  or or_5 (or_5_out, and_20_out, and_21_out, and_22_out, and_23_out, and_24_out, and_25_out, and_26_out, and_27_out);

  // Notes on the sheet:
  //   II PARTE. SIMULACIÓN DE COMPUERTA AND
  //   III PARTE. SIMULACIÓN DE COMPUERTA XOR
  //   IV PARTE. DECODIFICADOR
  //   F = AB' + A'B
  //   A'B'C'D'
  //   A'B'C'D
  //   A'B'CD'
  //   AB'CD
  //   A'BC'D'
  //   A'BC'D
  //   A'BCD'
  //   A'BCD
  //   AB'C'D'
  //   AB'C'D
  //   AB'CD'
  //   ABC'D'
  //   ABC'D
  //   ABCD'
  //   ABCD
  //   A'B'CD
  //   IV PARTE. CODIFICADOR
  //   IV PARTE. MULTIPLEXOR
  //   y
  //   x
  //   V
  //   Y
endmodule
